# Fritzing sketch Project (saved by Fritzing 0.9.8b)

parts:
  D1 = SOLAR-IXYS [package=solarbit-12x1]
  Part3 = Audio FX Sound Board + 2x2W Amp
  Part1 = Arduino Portenta
  SPKR1 = Loudspeaker

nets:
  VIN: D1.A, Part3.VIN, Part1.+5V
  GND: D1.C, Part3.GND, Part1.GND
  N1: Part3.TX, Part1.UART1_RX
  N2: Part3.RX, Part1.UART1_TX
  N3: Part3.L-, SPKR1.pin1

custom parts:
  Audio FX Sound Board + 2x2W Amp: The Adafruit Sound Board, the fastest way to add audio effects to a project!
  Arduino Portenta: The Arduino Nano is a small, complete, and breadboard-friendly board based on the ATmega328 (Arduino Nano 3.0) or ATmega168 (Arduino Nano 2.x). It has more or less the same functionality of the Arduino Duemilanove, but in a different package. It lacks only a DC power jack, and works with a Mini-B USB cable instead of a standard one. The Nano was designed and is being produced by Gravitech.
